# Fritzing sketch Matrix (saved by Fritzing 0.9.4)
breadboards: 2

parts:
  Bauteil1 = Arduino Uno (Rev3)
  R4 = Resistor [tolerance=±5% resistance=1k package=THT]
  R5 = Resistor [tolerance=±5% resistance=1k package=THT]
  Disp1 = LBT2088AH [part_number=LBT2088AH]
  R6 = Resistor [tolerance=±5% resistance=1k package=THT]
  R7 = Resistor [tolerance=±5% resistance=1k package=THT]
  R8 = Resistor [tolerance=±5% resistance=1k package=THT]  # not connected
  R9 = Resistor [tolerance=±5% resistance=1k package=THT]
  R10 = Resistor [tolerance=±5% resistance=1k package=THT]  # not connected
  R11 = Resistor [tolerance=±5% resistance=1k package=THT]  # not connected
  R12 = Resistor [tolerance=±5% resistance=1k package=THT]  # not connected
  R13 = Resistor [tolerance=±5% resistance=1k package=THT]
  R14 = Resistor [tolerance=±5% resistance=1k package=THT]
  R15 = Resistor [tolerance=±5% resistance=1k package=THT]

nets:
  N1: Bauteil1.A0, R7.Pin_0
  N2: Bauteil1.A1, R9.Pin_0
  N3: Bauteil1.A2, Disp1.pin_14
  N4: Bauteil1.A3, R6.Pin_0
  N5: Bauteil1.D8, Disp1.pin_5
  N6: Bauteil1.D9_PWM, R14.Pin_1
  N7: Bauteil1.D10_PWM/SS, R13.Pin_1
  N8: Bauteil1.D11_PWM/MOSI, Disp1.pin2
  N9: Bauteil1.D12/MISO, Disp1.pin1
  N10: Bauteil1.D0/RX, Disp1.pin_12
  N11: Bauteil1.D1/TX, R5.Pin_0
  N12: Bauteil1.D3_PWM, R4.Pin_0
  N13: Bauteil1.D4, Disp1.pin_9
  N14: Bauteil1.D5_PWM, Disp1.pin_8
  N15: Bauteil1.D6_PWM, Disp1.pin_7
  N16: Bauteil1.D7, R15.Pin_1
  N17: R4.Pin_1, Disp1.pin_10
  N18: R5.Pin_1, Disp1.pin_11
  N19: Disp1.pin_3, R13.Pin_0
  N20: Disp1.pin_4, R14.Pin_0
  N21: Disp1.pin_6, R15.Pin_0
  N22: Disp1.pin_13, R6.Pin_1
  N23: Disp1.pin_15, R9.Pin_1
  N24: Disp1.pin_16, R7.Pin_1

notes:
  Blau: Plus (Anode) - Anschluss
  Orange: Minus (Kathode) - Anschluss
  (Wichtig: 1K Ohm Widerstand benötigt)
